# Fritzing sketch Tabela_acessivel_arduino_dfplayer (saved by Fritzing 1.0.4)
circuit board: 8.46667cm x 5.64444cm

parts:
  Arduino_UNO_R3 = Arduino Uno (Rev3)
  Joystick = Thumb Joystick
  S1 = Round Pushbutton
  R1 = Resistor [tolerance=±5% resistance=330 package="2010 [SMD]"]
  U1 = 2.5mm Audio Jack [package=stereojack2.5mm_specia_pogopins]
  VCC1 = Battery block 9V [internal_resistance=0.1Ω]
  Step_Down = RioRand LM2596
  DFRobot_DFPlayer_Mini1 = DFRobot DFPlayer Mini [part_number=DFR0299]
  SP1 = SPEAKER [package=pcb_mount_speaker]

nets:
  N1: Arduino_UNO_R3.A0, Joystick.HORZ
  N2: Arduino_UNO_R3.A1, Joystick.VERT
  N3: Arduino_UNO_R3.D10_PWM/SS, DFRobot_DFPlayer_Mini1.TX
  N4: Arduino_UNO_R3.D11_PWM/MOSI, R1.Pin_0
  GND: Arduino_UNO_R3.GND, Joystick.GND, S1.leg0, U1.SLEEVE, Step_Down.Pin_4, SP1.+
  N5: Arduino_UNO_R3.D5_PWM, U1.RIGHT, DFRobot_DFPlayer_Mini1.DAC_R
  N6: Arduino_UNO_R3.D6_PWM, Joystick.SEL
  N7: Arduino_UNO_R3.D7, S1.leg1
  3V3: Arduino_UNO_R3.3V3, DFRobot_DFPlayer_Mini1.VCC
  5V: Arduino_UNO_R3.5V, Joystick.VCC
  N8: Arduino_UNO_R3.VIN, Step_Down.Pin_3
  N9: R1.Pin_1, DFRobot_DFPlayer_Mini1.RX
  N10: U1.LEFT, DFRobot_DFPlayer_Mini1.DAC_L
  N11: VCC1.-, Step_Down.Pin_2
  N12: VCC1.+, Step_Down.Pin_1
  N13: DFRobot_DFPlayer_Mini1.SPK_2, SP1.-
